// Logisim project Control_Unit.circ as structural Verilog
module Control_Unit (
  input  START,
  input  FETCHED,
  input  EXECUTED,
  input  HALT,
  input  RESET,
  input  [2:0] Instruction_Type,
  output fetch,
  output reset_2
);

  wire clk, demultiplexer_1_out0, demultiplexer_2_out0, demultiplexer_2_out1, demultiplexer_3_out0,
       demultiplexer_3_out1, demultiplexer_4_out0, demultiplexer_4_out1, demultiplexer_4_out2,
       demultiplexer_4_out4, demultiplexer_4_out5, demultiplexer_4_out6, demultiplexer_4_out7,
       demultiplexer_5_out0, demultiplexer_5_out1, END_q, EXEC_q, FETCH_q, IDLE_q, or_1_out, or_2_out,
       or_3_out, or_4_out;

  Clock clock_1 (.out(clk));
  or or_1 (or_1_out, demultiplexer_1_out0, 1'b1);
  Demultiplexer #(.enable("false")) demultiplexer_1 (
    .out0(demultiplexer_1_out0), .out1(fetch), .in(IDLE_q), .sel(START));
  D_Flip_Flop IDLE (.clk(or_1_out), .D(clk), .Q(IDLE_q), .preset(1'b1));  // open: Qn, en, reset
  or or_2 (or_2_out, demultiplexer_2_out0, demultiplexer_5_out1, fetch);
  D_Flip_Flop u_FETCH (.clk(or_2_out), .D(clk), .Q(FETCH_q), .preset(1'b1));  // open: Qn, en, reset
  Demultiplexer #(.enable("false")) demultiplexer_2 (
    .out0(demultiplexer_2_out0), .out1(demultiplexer_2_out1), .in(FETCH_q), .sel(FETCHED));
  Demultiplexer #(.enable("false")) demultiplexer_3 (
    .out0(demultiplexer_3_out0), .out1(demultiplexer_3_out1), .in(demultiplexer_2_out1), .sel(HALT));
  Demultiplexer #(.select(3), .enable("false")) demultiplexer_4 (
    .out0(demultiplexer_4_out0), .out1(demultiplexer_4_out1), .out2(demultiplexer_4_out2),
    .out3(demultiplexer_4_out2), .out4(demultiplexer_4_out4), .out5(demultiplexer_4_out5),
    .out6(demultiplexer_4_out6), .out7(demultiplexer_4_out7), .in(demultiplexer_3_out0),
    .sel(Instruction_Type));
  or or_3 (or_3_out, demultiplexer_5_out0, demultiplexer_3_out0);
  D_Flip_Flop EXEC (.clk(or_3_out), .D(clk), .Q(EXEC_q), .preset(1'b1));  // open: Qn, en, reset
  Demultiplexer #(.enable("false")) demultiplexer_5 (
    .out0(demultiplexer_5_out0), .out1(demultiplexer_5_out1), .in(EXEC_q), .sel(EXECUTED));
  or or_4 (or_4_out, END_q, demultiplexer_3_out1);
  D_Flip_Flop END (.clk(or_4_out), .D(clk), .Q(END_q), .preset(1'b1));  // open: Qn, en, reset

  assign reset_2 = RESET;

  // Other names for the same wires on the sheet: Op_Type[2:0] = Instruction_Type; rst = RESET

  // Notes on the sheet:
  //   Grupo A
  //   GrupoB
  //   Grupo C
  //   Grupo D
  //   Grupo E
  //   Grupo E
  //   Grupo Pop Push
  //   Grupo Gei
  //   Enviar bit al DataPath para decidir entre rt y rd
  //   (1-Mandar al ALU a revisar condicion (esto ya pasa)
  //   pop
  //   push
  //   Separar enload y store y hacer lo que hac pop y push
  //   3- MAndar un bit para dejar pasar la constante A en el BC como jmp addrs
  //   Pasarle un write en R/W
  //   poner el ultimo bit del instruction aqui (el menos signif)
  //   2- enviar un bir al multiplex del flag ocndition del BC para que deje pasar el resultado de la alu y enviar un 1 al jump
  //   acceder al RF y obtener Sp
  //   Pasarle SP al Memory Manager
  //   crear un estado para esperar el updated del memory
  //   ese bit en 0 es pop y en 1 push
  //   Hacer exatamente lo que hice en el componente GEI
  //   pasarle un bit al multiplexer de data input en el register file que ese multiplexer va aa tener entre sus opciones el valor de entrada de memoria que recibe data path 
endmodule
